# Fritzing sketch delphine (saved by Fritzing 0.9.3b)
circuit board: 8.46667cm x 5.64444cm
breadboards: 1

parts:
  PIR1 = PIR sensor
  Part1 = Arduino Uno (Rev3) - ICSP
  J2 = Basic Servo
  J3 = Piezo Speaker

nets:
  VDD: PIR1.VDD, Part1.5V, J2.vcc
  GND: PIR1.GND, Part1.GND, J2.gnd, J3.pin1
  N1: Part1.D6_PWM, J3.pin2

// code stored in the sketch: DEL.ino
#include <Servo.h>

// constants won't change
const int MOTION_SENSOR_PIN = 6; // Arduino pin connected to motion sensor's pinj
const int SERVO_PIN         = 8; // Arduino pin connected to servo motor's pin

Servo servo; 
int angle = 0;          // the current angle of servo motor
int lastMotionState;    // the previous state of motion sensor
int currentMotionState; // the current state of motion sensor
int buzzer=4;
void setup() {
  Serial.begin(9600);                // initialize serial
  pinMode(MOTION_SENSOR_PIN, INPUT); // set arduino pin to input mode
  servo.attach(SERVO_PIN);           // attaches the servo on pin 9 to the servo object
 pinMode(4,OUTPUT);
  servo.write(angle);
  currentMotionState = digitalRead(MOTION_SENSOR_PIN);
};

void loop() {
  lastMotionState    = currentMotionState;             // save the last state
  currentMotionState = digitalRead(MOTION_SENSOR_PIN); // read new state

  if (currentMotionState == HIGH && lastMotionState == LOW) { // pin state change: LOW -> HIGH
    Serial.println("Motion detected!");
    servo.write(180);
    digitalWrite(4,HIGH);
  }
  else
  if (currentMotionState == LOW && lastMotionState == HIGH)
  {
    Serial.println("Motion stopped!");
    servo.write(180);
    digitalWrite(4,LOW);
  }
}
